// Logisim project SAP_1.circ as structural Verilog: 6 circuits, main circuit main
module main (
  input  CLR,
  output [3:0] out_2,
  output [3:0] out_3,
  output Cout,
  output out_5,
  output out_6,
  output out_7,
  output out_8,
  output out_9,
  output out_10,
  output out_11,
  output out_12
);

  wire CLK, CLK_out, controller_1_t1, controller_1_t2, controller_1_t3, controller_1_t4, controller_1_t5,
       controller_1_t6, Cp, Ea, Ep, Eu, HLT, nCE, nEi, nLa, nLb, nLi, nLm, nLo, not_1_out, not_2_out,
       not_3_out, not_4_out, not_5_out, not_6_out, not_7_out, not_8_out, not_9_out, Su;
  wire [3:0] controlled_buffer_1_out, controlled_buffer_3_out, controlled_buffer_4_out,
       controlled_buffer_6_out, controlled_buffer_7_out, controlled_buffer_8_out, controlled_buffer_10_out,
       controlled_buffer_12_out, controlled_buffer_13_out, MAR_q, PC_q;
  wire [7:0] A_q, B_q, IR_q;

  not not_1 (not_1_out, nLi);
  assign controlled_buffer_1_out = not_1_out ? out_2 : 4'bz;  // Controlled_Buffer controlled_buffer_1
  not not_2 (not_2_out, nEi);
  Hex_Digit_Display hex_digit_display_1 (.value({Cp, Ep, nLm, nCE}));  // open: dp
  not not_3 (not_3_out, nLm);
  Hex_Digit_Display hex_digit_display_2 (.value({nLi, nEi, nLa, Ea}));  // open: dp
  Hex_Digit_Display hex_digit_display_3 (.value({Su, Eu, nLb, nLo}));  // open: dp
  Counter #(.width(4), .max('hf), .trigger("falling")) PC (
    .count(Cp), .Q(PC_q), .clk(not_4_out), .clr(CLR));  // open: load, D, carry
  assign out_3 = Ep ? PC_q : 4'bz;  // Controlled_Buffer controlled_buffer_2
  not not_4 (not_4_out, CLK);
  assign controlled_buffer_3_out = not_3_out ? out_3 : 4'bz;  // Controlled_Buffer controlled_buffer_3
  Register #(.width(4)) MAR (.D(controlled_buffer_3_out), .Q(MAR_q), .clk(CLK), .clr(CLR));  // open: en
  assign controlled_buffer_4_out = not_1_out ? out_3 : 4'bz;  // Controlled_Buffer controlled_buffer_4
  Register IR (.D({controlled_buffer_1_out, controlled_buffer_4_out}), .Q(IR_q), .clk(CLK), .clr(CLR));  // open: en
  not not_5 (not_5_out, nCE);
  RAM #(.addrWidth(4)) ram_1 (.addr(MAR_q), .data({out_2, out_3}), .ld(not_5_out));  // open: sel, clk, clr
  assign out_3 = not_2_out ? IR_q[3:0] : 4'bz;  // Controlled_Buffer controlled_buffer_5
  DotMatrix #(.matrixcols(6), .matrixrows(1)) dotmatrix_1 (
    .col0(controller_1_t6), .col1(controller_1_t5), .col2(controller_1_t4), .col3(controller_1_t3),
    .col4(controller_1_t2), .col5(controller_1_t1));
  Controller controller_1 (
    .I7_I6_I5_I4(IR_q[7:4]), .T6(controller_1_t6), .T5(controller_1_t5), .T4(controller_1_t4),
    .T3(controller_1_t3), .T2(controller_1_t2), .T1(controller_1_t1), .CLK(CLK), .nCLR(not_6_out), .HLT(HLT),
    .Cp(Cp), .Ep(Ep), .nLm(nLm), .nCE(nCE), .nLi(nLi), .nEi(nEi), .nLa(nLa), .Ea(Ea), .Su(Su), .Eu(Eu),
    .nLb(nLb), .nLo(nLo));
  Hex_Digit_Display hex_digit_display_4 (.value(out_2));  // open: dp
  not not_6 (not_6_out, CLR);
  Hex_Digit_Display hex_digit_display_5 (.value(out_3));  // open: dp
  Clock u_CLK (.out(CLK_out));
  assign controlled_buffer_6_out = not_8_out ? out_2 : 4'bz;  // Controlled_Buffer controlled_buffer_6
  assign controlled_buffer_7_out = not_9_out ? out_2 : 4'bz;  // Controlled_Buffer controlled_buffer_7
  assign controlled_buffer_8_out = not_7_out ? out_2 : 4'bz;  // Controlled_Buffer controlled_buffer_8
  assign CLK = HLT ? CLK_out : 1'bz;  // Controlled_Buffer controlled_buffer_9
  assign controlled_buffer_10_out = not_8_out ? out_3 : 4'bz;  // Controlled_Buffer controlled_buffer_10
  assign {out_2, out_3} = Ea ? A_q : 8'bz;  // Controlled_Buffer controlled_buffer_11
  assign controlled_buffer_12_out = not_9_out ? out_3 : 4'bz;  // Controlled_Buffer controlled_buffer_12
  not not_7 (not_7_out, nLo);
  assign controlled_buffer_13_out = not_7_out ? out_3 : 4'bz;  // Controlled_Buffer controlled_buffer_13
  Register A (.D({controlled_buffer_6_out, controlled_buffer_10_out}), .Q(A_q), .clk(CLK), .clr(CLR));  // open: en
  Register B (.D({controlled_buffer_7_out, controlled_buffer_12_out}), .Q(B_q), .clk(CLK), .clr(CLR));  // open: en
  Hex_Digit_Display hex_digit_display_6 (.value({out_5, out_6, out_7, out_8}));  // open: dp
  Register OUT (
    .D({controlled_buffer_8_out, controlled_buffer_13_out}),
    .Q({out_5, out_6, out_7, out_8, out_9, out_10, out_11, out_12}), .clk(CLK), .clr(CLR));  // open: en
  not not_8 (not_8_out, nLa);
  AdderSubtractor addersubtractor_1 (
    .out_6({out_2, out_3}), .A(A_q), .B(B_q), .Su(Su), .Eu(Eu), .Cout(Cout));  // open: Cin
  not not_9 (not_9_out, nLb);
  Hex_Digit_Display hex_digit_display_7 (.value({out_9, out_10, out_11, out_12}));  // open: dp

  // Notes on the sheet:
  //   W bus
endmodule

module Controller (
  input  nCLR,
  input  CLK,
  input  [3:0] I7_I6_I5_I4,
  output T6,
  output T5,
  output T4,
  output T3,
  output T2,
  output T1,
  output HLT,
  output Cp,
  output Ep,
  output nLm,
  output nCE,
  output nLi,
  output nEi,
  output nLa,
  output Ea,
  output Su,
  output Eu,
  output nLb,
  output nLo
);

  wire and_1_out, and_2_out, and_3_out, and_4_out, and_5_out, and_6_out, and_7_out, and_8_out, and_9_out,
       and_10_out, and_11_out, and_12_out, and_13_out, and_14_out, and_17_out, and_18_out, and_19_out,
       and_20_out, and_21_out, instructiondecoder_1_add, instructiondecoder_1_lda, instructiondecoder_1_out,
       instructiondecoder_1_sub, not_6_out, or_1_out, or_2_out, or_3_out, or_4_out, or_5_out, or_7_out;

  InstructionDecoder instructiondecoder_1 (
    .LDA(instructiondecoder_1_lda), .ADD(instructiondecoder_1_add), .SUB(instructiondecoder_1_sub),
    .OUT(instructiondecoder_1_out), .nHLT(HLT), .I7(I7_I6_I5_I4[3]), .I6(I7_I6_I5_I4[2]),
    .I5(I7_I6_I5_I4[1]), .I4(I7_I6_I5_I4[0]));
  Hex_Digit_Display hex_digit_display_1 (.value({Cp, Ep, nLm, nCE}));  // open: dp
  and and_1 (and_1_out, instructiondecoder_1_add, T4);
  and and_2 (and_2_out, instructiondecoder_1_lda, T4);
  or or_1 (or_1_out, Ep, and_2_out, and_1_out, and_4_out);
  Hex_Digit_Display hex_digit_display_2 (.value({nLi, nEi, nLa, Ea}));  // open: dp
  Hex_Digit_Display hex_digit_display_3 (.value({Su, Eu, nLb, nLo}));  // open: dp
  and and_3 (and_3_out, instructiondecoder_1_lda, T5);
  and and_4 (and_4_out, instructiondecoder_1_sub, T4);
  and and_5 (and_5_out, instructiondecoder_1_add, T5);
  not not_1 (nLm, or_1_out);
  and and_6 (and_6_out, instructiondecoder_1_sub, T5);
  and and_7 (and_7_out, instructiondecoder_1_lda, T4);
  or or_2 (or_2_out, T3, and_3_out, and_5_out, and_6_out);
  not not_2 (nLi, T3);
  not not_3 (nCE, or_2_out);
  RingCounter ringcounter_1 (.CLK(CLK), .CLR(or_5_out), .T6(T6), .T5(T5), .T4(T4), .T3(T3), .T2(Cp), .T1(Ep));
  and and_8 (and_8_out, instructiondecoder_1_add, T4);
  and and_9 (and_9_out, instructiondecoder_1_sub, T4);
  or or_3 (or_3_out, and_7_out, and_8_out, and_9_out);
  not not_4 (nLa, or_4_out);
  not not_5 (nEi, or_3_out);
  and and_10 (and_10_out, instructiondecoder_1_sub, T6);
  and and_11 (and_11_out, instructiondecoder_1_add, T6);
  and and_12 (and_12_out, instructiondecoder_1_lda, T5);
  or or_4 (or_4_out, and_12_out, and_11_out, and_10_out);
  not not_6 (not_6_out, nCLR);
  and and_13 (and_13_out, T5, instructiondecoder_1_out);
  or or_5 (or_5_out, not_6_out, and_13_out, and_14_out);
  and and_14 (and_14_out, T6, instructiondecoder_1_lda);
  and and_15 (Ea, instructiondecoder_1_out, T4);
  and and_16 (Su, instructiondecoder_1_sub, T6);
  not not_7 (nLb, or_7_out);
  not not_8 (nLo, and_21_out);
  and and_17 (and_17_out, instructiondecoder_1_sub, T6);
  and and_18 (and_18_out, instructiondecoder_1_add, T6);
  or or_6 (Eu, and_18_out, and_17_out);
  and and_19 (and_19_out, instructiondecoder_1_add, T5);
  and and_20 (and_20_out, instructiondecoder_1_sub, T5);
  and and_21 (and_21_out, instructiondecoder_1_out, T4);
  or or_7 (or_7_out, and_19_out, and_20_out);

  assign T1 = Ep;
  assign T2 = Cp;
endmodule

module RingCounter (
  input  CLK,
  input  CLR,
  output T6,
  output T5,
  output T4,
  output T3,
  output T2,
  output T1
);

  wire j_k_ff_1_qn, j_k_ff_2_qn, j_k_ff_3_qn, j_k_ff_4_qn, j_k_ff_5_qn, j_k_ff_6_q;

  J_K_Flip_Flop #(.trigger("falling")) j_k_ff_1 (
    .J(T5), .clk(CLK), .K(j_k_ff_2_qn), .Q(T6), .Qn(j_k_ff_1_qn), .reset(CLR));  // open: preset, en
  J_K_Flip_Flop #(.trigger("falling")) j_k_ff_2 (
    .J(T4), .clk(CLK), .K(j_k_ff_3_qn), .Q(T5), .Qn(j_k_ff_2_qn), .reset(CLR));  // open: preset, en
  J_K_Flip_Flop #(.trigger("falling")) j_k_ff_3 (
    .J(T3), .clk(CLK), .K(j_k_ff_4_qn), .Q(T4), .Qn(j_k_ff_3_qn), .reset(CLR));  // open: preset, en
  J_K_Flip_Flop #(.trigger("falling")) j_k_ff_4 (
    .J(T2), .clk(CLK), .K(j_k_ff_5_qn), .Q(T3), .Qn(j_k_ff_4_qn), .reset(CLR));  // open: preset, en
  J_K_Flip_Flop #(.trigger("falling")) j_k_ff_5 (
    .J(T1), .clk(CLK), .K(j_k_ff_6_q), .Q(T2), .Qn(j_k_ff_5_qn), .reset(CLR));  // open: preset, en
  J_K_Flip_Flop #(.trigger("falling")) j_k_ff_6 (
    .J(j_k_ff_1_qn), .clk(CLK), .K(T6), .Q(j_k_ff_6_q), .Qn(T1), .reset(CLR));  // open: preset, en
endmodule

module InstructionDecoder (
  input  I7,
  input  I6,
  input  I5,
  input  I4,
  output LDA,
  output ADD,
  output SUB,
  output OUT,
  output nHLT
);

  wire and_5_out, not_1_out, not_2_out, not_3_out, not_4_out;

  not not_1 (not_1_out, I5);
  not not_2 (not_2_out, I6);
  not not_3 (not_3_out, I7);
  not not_4 (not_4_out, I4);
  and and_1 (LDA, not_3_out, not_2_out, not_1_out, not_4_out);
  and and_2 (ADD, not_3_out, not_2_out, not_1_out, I4);
  and and_3 (SUB, not_3_out, not_2_out, I5, not_4_out);
  and and_4 (OUT, I7, I6, I5, not_4_out);
  and and_5 (and_5_out, I7, I6, I5, I4);
  not not_5 (nHLT, and_5_out);
endmodule

module ProgramCounter (
  input  Cp,
  input  nCLR,
  input  nCLK,
  input  in_4,
  input  in_5,
  input  in_6,
  input  [5:0] in_7,
  input  [2:0] in_8,
  output out_9,
  output out_10,
  output out_11,
  output out_12,
  output [3:0] out_13,
  output [5:0] out_14
);

  wire not_1_out, not_2_out, not_3_out, not_4_out;

  J_K_Flip_Flop #(.trigger("falling")) j_k_ff_1 (
    .J(Cp), .clk(out_10), .K(Cp), .Q(out_9), .reset(not_3_out));  // open: Qn, preset, en
  not not_1 (not_1_out, in_5);
  J_K_Flip_Flop #(.trigger("falling")) j_k_ff_2 (
    .J(Cp), .clk(out_11), .K(Cp), .Q(out_10), .reset(not_3_out));  // open: Qn, preset, en
  Counter #(.width(4), .max('hf), .trigger("falling")) counter_1 (
    .count(in_4), .Q(out_13), .clk(not_1_out), .clr(not_2_out));  // open: load, D, carry
  not not_2 (not_2_out, in_6);
  J_K_Flip_Flop #(.trigger("falling")) j_k_ff_3 (
    .J(Cp), .clk(out_12), .K(Cp), .Q(out_11), .reset(not_3_out));  // open: Qn, preset, en
  Shifter #(.width(6)) shifter_1 (.in(in_7), .\dist (in_8), .out(out_14));
  J_K_Flip_Flop #(.trigger("falling")) j_k_ff_4 (
    .J(Cp), .clk(not_4_out), .K(Cp), .Q(out_12), .reset(not_3_out));  // open: Qn, preset, en
  not not_3 (not_3_out, nCLR);
  not not_4 (not_4_out, nCLK);
endmodule

module AdderSubtractor (
  input  [7:0] A,
  input  [7:0] B,
  input  Cin,
  input  Eu,
  input  Su,
  output [7:0] out_6,
  output Cout
);

  wire adder_1_cout, subtractor_1_bout;
  wire [7:0] adder_1_out, multiplexer_1_out, subtractor_1_out;

  Hex_Digit_Display hex_digit_display_1 (.value(A[7:4]));  // open: dp
  Adder adder_1 (.a(A), .b(B), .out(adder_1_out), .cin(Cin), .cout(adder_1_cout));
  Subtractor subtractor_1 (.a(A), .b(B), .out(subtractor_1_out), .bin(Cin), .bout(subtractor_1_bout));
  Hex_Digit_Display hex_digit_display_2 (.value(A[3:0]));  // open: dp
  Hex_Digit_Display hex_digit_display_3 (.value(B[7:4]));  // open: dp
  assign out_6 = Eu ? multiplexer_1_out : 8'bz;  // Controlled_Buffer controlled_buffer_1
  Multiplexer #(.width(8), .enable("false")) multiplexer_1 (
    .in0(adder_1_out), .in1(subtractor_1_out), .out(multiplexer_1_out), .sel(Su));
  Multiplexer #(.enable("false")) multiplexer_2 (.in0(adder_1_cout), .in1(subtractor_1_bout), .out(Cout), .sel(Su));
  Hex_Digit_Display hex_digit_display_4 (.value(B[3:0]));  // open: dp
  Hex_Digit_Display hex_digit_display_5 (.value(out_6[7:4]));  // open: dp
  Hex_Digit_Display hex_digit_display_6 (.value(out_6[3:0]));  // open: dp
endmodule
